// Logisim project HW4-The final edition.circ as structural Verilog: 6 circuits, main circuit register
module CPU (
  input  in_1,
  input  in_2
);

  wire alu_1_zero, and_1_out, and_2_out, clock_1_out, clock_2_out, clock_3_out, control_1_alusrc,
       control_1_branch, control_1_call, control_1_halt, control_1_immediate, control_1_load,
       control_1_memtoreg, control_1_regdst, control_1_regwrite, control_1_return, control_1_store,
       control_1_zero, not_1_out, or_1_out;
  wire [2:0] alucontrol_1_aluselector, multiplexer_2_out;
  wire [3:0] control_1_aluselector;
  wire [15:0] add_or_sub_1_out_4, adder_1_out, alu_1_out_5, bit_extender_1_out, multiplexer_1_out,
       multiplexer_3_out, multiplexer_4_out, multiplexer_5_out, multiplexer_6_out, PC_q, ra_q, ram_1_data,
       register_file_data1, register_file_data2, rom_1_data;

  Clock clock_1 (.out(clock_1_out));
  Clock clock_2 (.out(clock_2_out));
  Register #(.width(16)) ra (.D(adder_1_out), .en(control_1_call), .Q(ra_q), .clk(clock_1_out));  // open: clr
  Multiplexer #(.width(16), .enable("false")) multiplexer_1 (
    .in0(multiplexer_5_out), .in1(ra_q), .out(multiplexer_1_out), .sel(control_1_return));
  and and_1 (and_1_out, clock_2_out, not_1_out);
  Register #(.width(16)) PC (.D(multiplexer_1_out), .en(1'b1), .Q(PC_q), .clk(and_1_out));  // open: clr
  Adder #(.width(16)) adder_1 (.a(16'h1), .b(PC_q), .out(adder_1_out));  // open: cin, cout
  not not_1 (not_1_out, control_1_halt);
  ROM #(.addrWidth(16), .dataWidth(16)) rom_1 (.addr(PC_q), .data(rom_1_data), .sel(1'b1));
  CONTROL control_1 (
    .in_1(rom_1_data[15:12]), .Branch(control_1_branch), .ALUSelector(control_1_aluselector),
    .RegWrite(control_1_regwrite), .ALUSrc(control_1_alusrc), .MemtoReg(control_1_memtoreg),
    .RegDst(control_1_regdst), .Halt(control_1_halt), .Store(control_1_store), .Load(control_1_load),
    .Call(control_1_call), .Return(control_1_return), .ZERO(control_1_zero), .IMMEDIATE(control_1_immediate));
  // Probe on multiplexer_6_out
  // Probe on multiplexer_2_out
  Multiplexer #(.width(3), .enable("false")) multiplexer_2 (
    .in0(rom_1_data[5:3]), .in1(rom_1_data[8:6]), .out(multiplexer_2_out), .sel(control_1_regdst));
  assign bit_extender_1_out = {{10{1'b0}}, rom_1_data[5:0]};  // Bit_Extender bit_extender_1
  register register_file (
    .Write(control_1_regwrite), .Write_Register(multiplexer_2_out), .Register_Data(multiplexer_6_out),
    .clock(and_1_out), .reset(in_2), .Read_Regisiter1(rom_1_data[8:6]), .Read_Regisiter2(rom_1_data[11:9]),
    .Data1(register_file_data1), .Data2(register_file_data2));
  // Probe on register_file_data1
  Multiplexer #(.width(16), .enable("false")) multiplexer_3 (
    .in0(register_file_data2), .in1(bit_extender_1_out), .out(multiplexer_3_out), .sel(control_1_alusrc));
  Multiplexer #(.width(16)) multiplexer_4 (
    .in0(register_file_data1), .in1(register_file_data2), .out(multiplexer_4_out), .sel(control_1_immediate));  // open: en
  ALUControl alucontrol_1 (.in_1(control_1_aluselector), .ALUSelector(alucontrol_1_aluselector));
  Multiplexer #(.width(16), .enable("false")) multiplexer_5 (
    .in0(adder_1_out), .in1(add_or_sub_1_out_4), .out(multiplexer_5_out), .sel(and_2_out));
  add_or_sub add_or_sub_1 (.in_1(PC_q), .in_2(bit_extender_1_out), .sign(rom_1_data[5]), .out_4(add_or_sub_1_out_4));
  and and_2 (and_2_out, control_1_branch, or_1_out);
  or or_1 (or_1_out, control_1_zero, alu_1_zero);
  ALU alu_1 (
    .data1(multiplexer_4_out), .data2(multiplexer_3_out), .ALUSelector(alucontrol_1_aluselector),
    .zero(alu_1_zero), .out_5(alu_1_out_5));
  // Probe on multiplexer_3_out
  // Probe on multiplexer_5_out
  // Probe on register_file_data2
  // Probe on alu_1_out_5
  Clock clock_3 (.out(clock_3_out));
  RAM #(.addrWidth(16), .dataWidth(16), .bus("separate")) ram_1 (
    .addr(alu_1_out_5), .din(register_file_data2), .data(ram_1_data), .str(control_1_store), .sel(1'b1),
    .clk(clock_3_out), .ld(control_1_load), .clr(in_1));
  Multiplexer #(.width(16), .enable("false")) multiplexer_6 (
    .in0(ram_1_data), .in1(alu_1_out_5), .out(multiplexer_6_out), .sel(control_1_memtoreg));
  // Probe on multiplexer_6_out

  // Notes on the sheet:
  //   **check halt
  //   contents of rom_1 (hex, n*v repeats v):
  //   1006 1044 f007 74c0 1007 f003 7500 d003 4210 e000 6*0 111
endmodule

module register (
  input  [2:0] Read_Regisiter1,
  input  Write,
  input  [2:0] Read_Regisiter2,
  input  [2:0] Write_Register,
  input  [15:0] Register_Data,
  input  clock,
  input  reset,
  output [15:0] Data1,
  output [15:0] Data2
);

  wire and_1_out, and_2_out, and_3_out, and_4_out, and_5_out, and_6_out, and_7_out, and_8_out,
       decoder_1_out0, decoder_1_out1, decoder_1_out2, decoder_1_out3, decoder_1_out4, decoder_1_out5,
       decoder_1_out6, decoder_1_out7;
  wire [15:0] register_1_q, register_2_q, register_3_q, register_4_q, register_5_q, register_6_q,
       register_7_q, register_8_q;

  Decoder #(.select(3), .enable("false")) decoder_1 (
    .out0(decoder_1_out0), .out1(decoder_1_out1), .out2(decoder_1_out2), .out3(decoder_1_out3),
    .out4(decoder_1_out4), .out5(decoder_1_out5), .out6(decoder_1_out6), .out7(decoder_1_out7),
    .sel(Write_Register));
  and and_1 (and_1_out, Write, decoder_1_out0);
  and and_2 (and_2_out, Write, decoder_1_out1);
  and and_3 (and_3_out, Write, decoder_1_out2);
  and and_4 (and_4_out, Write, decoder_1_out3);
  and and_5 (and_5_out, Write, decoder_1_out4);
  and and_6 (and_6_out, Write, decoder_1_out5);
  and and_7 (and_7_out, Write, decoder_1_out6);
  and and_8 (and_8_out, Write, decoder_1_out7);
  Register #(.width(16)) register_1 (.D(Register_Data), .en(and_1_out), .Q(register_1_q), .clk(clock), .clr(reset));
  Register #(.width(16)) register_2 (.D(Register_Data), .en(and_2_out), .Q(register_2_q), .clk(clock), .clr(reset));
  Register #(.width(16)) register_3 (.D(Register_Data), .en(and_3_out), .Q(register_3_q), .clk(clock), .clr(reset));
  Register #(.width(16)) register_4 (.D(Register_Data), .en(and_4_out), .Q(register_4_q), .clk(clock), .clr(reset));
  Register #(.width(16)) register_5 (.D(Register_Data), .en(and_5_out), .Q(register_5_q), .clk(clock), .clr(reset));
  Register #(.width(16)) register_6 (.D(Register_Data), .en(and_6_out), .Q(register_6_q), .clk(clock), .clr(reset));
  Register #(.width(16)) register_7 (.D(Register_Data), .en(and_7_out), .Q(register_7_q), .clk(clock), .clr(reset));
  Register #(.width(16)) register_8 (.D(Register_Data), .en(and_8_out), .Q(register_8_q), .clk(clock), .clr(reset));
  Multiplexer #(.select(3), .width(16)) multiplexer_1 (
    .in0(register_1_q), .in1(register_2_q), .in2(register_3_q), .in3(register_4_q), .in4(register_5_q),
    .in5(register_6_q), .in6(register_7_q), .in7(register_8_q), .out(Data1), .sel(Read_Regisiter1));  // open: en
  Multiplexer #(.select(3), .width(16)) multiplexer_2 (
    .in0(register_1_q), .in1(register_2_q), .in2(register_3_q), .in3(register_4_q), .in4(register_5_q),
    .in5(register_6_q), .in6(register_7_q), .in7(register_8_q), .out(Data2), .sel(Read_Regisiter2));  // open: en

  // Notes on the sheet:
  //   replaced
endmodule

module ALU (
  input  [15:0] data1,
  input  [15:0] data2,
  input  [2:0] ALUSelector,
  output zero,
  output [15:0] out_5
);

  wire comparator_1_gt, comparator_2_eq, not_1_out, not_2_out, not_3_out;
  wire [15:0] adder_1_out, and_1_out, or_1_out;

  Comparator #(.width(16), .mode("unsigned")) comparator_1 (
    .a(data1), .b(data2), .gt(comparator_1_gt));  // open: eq, lt
  not not_1 (not_1_out, comparator_1_gt);
  Comparator #(.width(16)) comparator_2 (.a(data1), .b(data2), .eq(comparator_2_eq));  // open: gt, lt
  not not_2 (not_2_out, comparator_2_eq);
  Adder #(.width(16)) adder_1 (.a(data1), .b(data2), .out(adder_1_out), .cin(1'b0));  // open: cout
  assign and_1_out = data1 & data2;  // AND_Gate and_1, 16 bits wide
  assign or_1_out = data1 | data2;  // OR_Gate or_1, 16 bits wide
  not not_3 (not_3_out, ALUSelector[0]);
  Multiplexer multiplexer_1 (.in0(not_2_out), .in1(not_1_out), .out(zero), .sel(not_3_out));  // open: en
  Multiplexer #(.select(3), .width(16), .enable("false")) multiplexer_2 (
    .in0(adder_1_out), .in1(and_1_out), .in2(or_1_out), .in3(data2), .in4(data1), .out(out_5),
    .sel(ALUSelector));  // open: in5, in6, in7

  // Notes on the sheet:
  //   xx0 ble / xx1 bne
  //   ble
  //   bne
endmodule

module ALUControl (
  input  [3:0] in_1,
  output [2:0] ALUSelector
);

  wire ADD, AND, and_1_out, and_2_out, and_3_out, and_4_out, and_5_out, and_6_out, ble_out, bne_out, LI_out,
       LOAD_out, MOVE_out, not_1_out, not_2_out, not_3_out, not_4_out, not_5_out, not_6_out, not_7_out,
       not_8_out, not_9_out, not_10_out, not_11_out, not_12_out, not_13_out, not_14_out, not_15_out,
       not_16_out, not_17_out, not_18_out, not_19_out, not_20_out, not_21_out, not_22_out, not_23_out,
       not_24_out, not_25_out, not_26_out, OR, or_1_out, or_2_out, Store_out;
  wire [2:0] and_7_out, and_8_out, and_9_out, and_10_out, and_11_out, and_12_out, bit_extender_1_out,
       bit_extender_2_out, bit_extender_3_out, bit_extender_4_out, bit_extender_5_out, bit_extender_6_out;

  not not_1 (not_1_out, in_1[3]);
  not not_2 (not_2_out, in_1[2]);
  not not_3 (not_3_out, in_1[0]);
  not not_4 (not_4_out, in_1[3]);
  not not_5 (not_5_out, in_1[3]);
  not not_6 (not_6_out, in_1[2]);
  not not_7 (not_7_out, in_1[1]);
  not not_8 (not_8_out, in_1[2]);
  not not_9 (not_9_out, in_1[1]);
  not not_10 (not_10_out, in_1[2]);
  not not_11 (not_11_out, in_1[1]);
  not not_12 (not_12_out, in_1[0]);
  not not_13 (not_13_out, in_1[3]);
  not not_14 (not_14_out, in_1[2]);
  and LOAD (LOAD_out, not_1_out, not_2_out, in_1[1], not_3_out);
  and MOVE (MOVE_out, not_4_out, in_1[2], in_1[1], in_1[0]);
  and LI (LI_out, not_5_out, not_6_out, not_7_out, in_1[0]);
  and bne (bne_out, in_1[3], not_8_out, not_9_out, in_1[0]);
  and ble (ble_out, in_1[3], not_10_out, not_11_out, not_12_out);
  and Store (Store_out, not_13_out, not_14_out, in_1[1], in_1[0]);
  assign bit_extender_1_out = {{2{or_1_out}}, or_1_out};  // Bit_Extender bit_extender_1
  or or_1 (or_1_out, LOAD_out, MOVE_out, LI_out);
  assign bit_extender_2_out = {{2{bne_out}}, bne_out};  // Bit_Extender bit_extender_2
  assign bit_extender_3_out = {{2{or_2_out}}, or_2_out};  // Bit_Extender bit_extender_3
  or or_2 (or_2_out, ble_out, Store_out);
  assign bit_extender_4_out = {{2{OR}}, OR};  // Bit_Extender bit_extender_4
  assign bit_extender_5_out = {{2{AND}}, AND};  // Bit_Extender bit_extender_5
  assign bit_extender_6_out = {{2{ADD}}, ADD};  // Bit_Extender bit_extender_6
  not not_15 (not_15_out, in_1[3]);
  not not_16 (not_16_out, in_1[0]);
  not not_17 (not_17_out, in_1[1]);
  not not_18 (not_18_out, in_1[0]);
  and and_1 (and_1_out, not_15_out, in_1[2], in_1[1], not_16_out);
  and and_2 (and_2_out, in_1[3], in_1[2], not_17_out, not_18_out);
  not not_19 (not_19_out, in_1[3]);
  and and_3 (and_3_out, not_19_out, in_1[2], not_20_out, in_1[0]);
  not not_20 (not_20_out, in_1[1]);
  not not_21 (not_21_out, in_1[2]);
  and and_4 (and_4_out, in_1[3], not_21_out, in_1[1], in_1[0]);
  not not_22 (not_22_out, in_1[3]);
  and and_5 (and_5_out, not_22_out, in_1[2], not_23_out, not_24_out);
  not not_23 (not_23_out, in_1[1]);
  not not_24 (not_24_out, in_1[0]);
  not not_25 (not_25_out, in_1[2]);
  and and_6 (and_6_out, in_1[3], not_25_out, in_1[1], not_26_out);
  not not_26 (not_26_out, in_1[0]);
  assign and_7_out = bit_extender_1_out & 3'b011;  // AND_Gate and_7, 3 bits wide
  assign and_8_out = bit_extender_2_out & 3'b101;  // AND_Gate and_8, 3 bits wide
  assign and_9_out = bit_extender_3_out & 3'b100;  // AND_Gate and_9, 3 bits wide
  assign and_10_out = bit_extender_4_out & 3'b010;  // AND_Gate and_10, 3 bits wide
  assign and_11_out = bit_extender_5_out & 3'b001;  // AND_Gate and_11, 3 bits wide
  assign and_12_out = bit_extender_6_out & 3'b000;  // AND_Gate and_12, 3 bits wide
  or or_3 (OR, and_1_out, and_2_out);
  or or_4 (AND, and_3_out, and_4_out);
  or or_5 (ADD, and_5_out, and_6_out);
  assign ALUSelector = and_7_out | and_8_out | and_9_out | and_10_out | and_11_out | and_12_out;  // OR_Gate or_6, 3 bits wide

  // Other names for the same wires on the sheet: OPCODE[3:0] = in_1
endmodule

module CONTROL (
  input  [3:0] in_1,
  output Branch,
  output [3:0] ALUSelector,
  output RegWrite,
  output ALUSrc,
  output MemtoReg,
  output RegDst,
  output Halt,
  output Store,
  output Load,
  output Call,
  output Return,
  output ZERO,
  output IMMEDIATE
);

  wire and_1_out, and_2_out, and_3_out, and_4_out, and_5_out, and_6_out, and_7_out, and_8_out, and_9_out,
       and_10_out, and_11_out, and_12_out, and_13_out, and_14_out, and_15_out, and_16_out, and_17_out,
       and_18_out, and_21_out, and_22_out, and_23_out, and_24_out, and_25_out, and_26_out, not_1_out,
       not_2_out, not_3_out, not_4_out, not_5_out, not_6_out, not_7_out, not_8_out, not_9_out, not_10_out,
       not_11_out, not_12_out, not_13_out, not_14_out, not_15_out, not_16_out, not_17_out, not_18_out,
       not_19_out, not_20_out, not_21_out, not_22_out, not_23_out, not_24_out, not_25_out, not_26_out,
       not_27_out, not_28_out, not_29_out, not_30_out, not_31_out, not_32_out, not_33_out, not_34_out,
       not_35_out, not_36_out, not_37_out, not_38_out, not_39_out, or_1_out, or_2_out, or_3_out, or_4_out,
       or_9_out;

  not not_1 (not_1_out, in_1[0]);
  not not_2 (not_2_out, in_1[0]);
  not not_3 (not_3_out, in_1[3]);
  not not_4 (not_4_out, in_1[1]);
  not not_5 (not_5_out, in_1[0]);
  not not_6 (not_6_out, in_1[2]);
  not not_7 (not_7_out, in_1[3]);
  not not_8 (not_8_out, in_1[2]);
  not not_9 (not_9_out, in_1[1]);
  not not_10 (not_10_out, in_1[1]);
  not not_11 (not_11_out, in_1[0]);
  not not_12 (not_12_out, in_1[3]);
  not not_13 (not_13_out, in_1[2]);
  not not_14 (not_14_out, in_1[3]);
  not not_15 (not_15_out, in_1[1]);
  not not_16 (not_16_out, in_1[1]);
  not not_17 (not_17_out, in_1[0]);
  not not_18 (not_18_out, in_1[1]);
  not not_19 (not_19_out, in_1[0]);
  not not_20 (not_20_out, in_1[2]);
  not not_21 (not_21_out, in_1[3]);
  not not_22 (not_22_out, in_1[3]);
  not not_23 (not_23_out, in_1[2]);
  or or_1 (or_1_out, in_1[1], in_1[0]);
  not not_24 (not_24_out, in_1[0]);
  not not_25 (not_25_out, in_1[2]);
  not not_26 (not_26_out, in_1[0]);
  and and_1 (and_1_out, in_1[1], in_1[2], in_1[3]);
  not not_27 (not_27_out, in_1[1]);
  and and_2 (and_2_out, in_1[3], not_27_out, in_1[0]);
  and and_3 (and_3_out, in_1[3], not_28_out, not_29_out);
  not not_28 (not_28_out, in_1[2]);
  not not_29 (not_29_out, in_1[1]);
  and and_4 (and_4_out, not_1_out, in_1[2], not_2_out);
  and and_5 (and_5_out, not_3_out, in_1[2]);
  not not_30 (not_30_out, in_1[3]);
  and and_6 (and_6_out, not_4_out, in_1[0]);
  or or_2 (or_2_out, and_6_out, and_7_out);
  and and_7 (and_7_out, in_1[1], not_5_out);
  not not_31 (not_31_out, in_1[2]);
  and and_8 (and_8_out, in_1[3], not_6_out, in_1[1]);
  and and_9 (and_9_out, not_7_out, not_8_out, not_9_out, in_1[0]);
  and and_10 (and_10_out, in_1[3], in_1[2], not_10_out, not_11_out);
  and and_11 (and_11_out, not_12_out, in_1[2]);
  and and_12 (and_12_out, in_1[3], not_13_out);
  and and_13 (and_13_out, not_14_out, not_15_out, in_1[0]);
  and and_14 (and_14_out, in_1[2], not_16_out, not_17_out);
  and and_15 (and_15_out, in_1[3], not_18_out, not_19_out);
  and and_16 (and_16_out, in_1[3], not_20_out);
  and and_17 (and_17_out, not_21_out, in_1[1], in_1[0]);
  and and_18 (and_18_out, not_22_out, not_23_out, or_1_out);
  or or_3 (or_3_out, in_1[0], in_1[1], in_1[2], in_1[3]);
  not not_32 (not_32_out, in_1[2]);
  not not_33 (not_33_out, in_1[3]);
  not not_34 (not_34_out, in_1[0]);
  not not_35 (not_35_out, in_1[2]);
  not not_36 (not_36_out, in_1[3]);
  and and_19 (Return, not_24_out, in_1[1], in_1[2], in_1[3]);
  or or_4 (or_4_out, in_1[0], in_1[1]);
  and and_20 (ZERO, or_4_out, and_21_out);
  and and_21 (and_21_out, in_1[2], in_1[3]);
  and and_22 (and_22_out, not_25_out, in_1[1], not_26_out);
  not not_37 (not_37_out, in_1[2]);
  and and_23 (and_23_out, not_37_out, in_1[0], in_1[1]);
  and and_24 (and_24_out, in_1[2], not_38_out, not_39_out);
  not not_38 (not_38_out, in_1[1]);
  not not_39 (not_39_out, in_1[0]);
  or or_5 (Branch, and_1_out, and_2_out, and_3_out);
  and and_25 (and_25_out, not_30_out, or_2_out);
  and and_26 (and_26_out, in_1[3], not_31_out, in_1[1]);
  or or_6 (ALUSrc, and_8_out, and_9_out, and_10_out);
  or or_7 (MemtoReg, and_11_out, and_12_out, and_13_out, and_14_out);
  or or_8 (RegDst, and_15_out, and_16_out, and_17_out, and_18_out);
  not not_40 (Halt, or_3_out);
  and and_27 (Store, in_1[0], in_1[1], not_32_out, not_33_out);
  and and_28 (Load, not_34_out, in_1[1], not_36_out);
  and and_29 (Call, in_1[0], in_1[1], in_1[3]);
  or or_9 (or_9_out, and_22_out, and_23_out, and_24_out);
  or or_10 (RegWrite, and_5_out, and_4_out, and_25_out, and_26_out);
  and and_30 (IMMEDIATE, or_9_out, in_1[3]);

  assign ALUSelector = in_1;

  // Other names for the same wires on the sheet: OPCODE[3:0] = in_1
endmodule

module add_or_sub (
  input  [15:0] in_1,
  input  [15:0] in_2,
  input  sign,
  output [15:0] out_4
);

  wire [5:0] adder_2_out, bit_extender_1_out, not_1_out;
  wire [15:0] adder_1_out, bit_extender_2_out, subtractor_1_out;

  Bit_Extender #(.in_width(16), .out_width(6)) bit_extender_1 (.in(in_2), .out(bit_extender_1_out));
  // Probe on bit_extender_1_out
  Adder #(.width(16)) adder_1 (.a(in_1), .b(in_2), .out(adder_1_out));  // open: cin, cout
  Subtractor #(.width(16)) subtractor_1 (.a(in_1), .b(bit_extender_2_out), .out(subtractor_1_out));  // open: bin, bout
  not not_1 (not_1_out[0], bit_extender_1_out[0]);
  not not_2 (not_1_out[1], bit_extender_1_out[1]);
  not not_3 (not_1_out[2], bit_extender_1_out[2]);
  not not_4 (not_1_out[3], bit_extender_1_out[3]);
  not not_5 (not_1_out[4], bit_extender_1_out[4]);
  not not_6 (not_1_out[5], bit_extender_1_out[5]);
  Multiplexer #(.width(16)) multiplexer_1 (
    .in0(adder_1_out), .in1(subtractor_1_out), .out(out_4), .sel(sign));  // open: en
  Adder #(.width(6)) adder_2 (.a(not_1_out), .b(6'b000001), .out(adder_2_out));  // open: cin, cout
  // Probe on adder_2_out
  assign bit_extender_2_out = {{10{1'b0}}, adder_2_out};  // Bit_Extender bit_extender_2
  // Probe on bit_extender_2_out

  // Notes on the sheet:
  //   5th bit
endmodule
